// Logisim project processador.circ as structural Verilog: 8 circuits, main circuit main
module main (
  input  RST
);

  wire ALU_SRC, ALU_ZERO, and_1_out, B_FLAG, CLK, JUMP, MEM_READ, MEM_TO_REG, MEM_WRITE, PC_SRC, R_WRITE,
       uc_1_branch;
  wire [1:0] IMM_SEL;
  wire [2:0] ALU_OP, FUNCT, instructiondecode_1_rd, instructiondecode_1_rs1, instructiondecode_1_rs2;
  wire [3:0] OPCODE;
  wire [5:0] instructiondecode_1_b_imm, instructiondecode_1_i_imm, instructiondecode_1_s_imm;
  wire [7:0] ALU_DATA, IMM, LINK_DATA, MEM_DATA, multiplexer_1_out, multiplexer_2_out, multiplexer_3_out,
       R_DATA2, registerfile_1_r_data1;
  wire [8:0] instructiondecode_1_j_imm;
  wire [15:0] instructionfetch_1_instruction;

  Clock u_CLK (.out(CLK));
  // Probe on instructionfetch_1_instruction
  // Probe on instructionfetch_1_instruction
  InstructionFetch instructionfetch_1 (
    .CLK(CLK), .RST(RST), .PC_SRC(PC_SRC), .IMM(IMM), .INSTRUCTION(instructionfetch_1_instruction),
    .LINK_DATA(LINK_DATA));
  Multiplexer #(.width(8)) multiplexer_1 (.in0(ALU_DATA), .in1(MEM_DATA), .out(multiplexer_1_out), .sel(MEM_TO_REG));
  Multiplexer #(.width(8)) multiplexer_2 (
    .in0(multiplexer_1_out), .in1(LINK_DATA), .out(multiplexer_2_out), .sel(JUMP));
  // Probe on multiplexer_2_out
  // Probe on multiplexer_2_out
  // Probe on multiplexer_2_out
  // Probe on multiplexer_2_out
  InstructionDecode instructiondecode_1 (
    .INSTRUCTION(instructionfetch_1_instruction), .RS1(instructiondecode_1_rs1),
    .RS2(instructiondecode_1_rs2), .RD(instructiondecode_1_rd), .OPCODE(OPCODE), .FUNCT(FUNCT),
    .I_IMM(instructiondecode_1_i_imm), .S_IMM(instructiondecode_1_s_imm), .B_IMM(instructiondecode_1_b_imm),
    .J_IMM(instructiondecode_1_j_imm));
  RegisterFile registerfile_1 (
    .CLK(CLK), .RST(RST), .DATA(multiplexer_2_out), .REG_WRITE(R_WRITE), .RS1(instructiondecode_1_rs1),
    .RS2(instructiondecode_1_rs2), .RD(instructiondecode_1_rd), .R_DATA1(registerfile_1_r_data1),
    .R_DATA2(R_DATA2));
  ImmGen immgen_1 (
    .I_IMM(instructiondecode_1_i_imm), .S_IMM(instructiondecode_1_s_imm), .B_IMM(instructiondecode_1_b_imm),
    .J_IMM(instructiondecode_1_j_imm), .IMM_SEL(IMM_SEL), .IMM(IMM));
  Multiplexer #(.width(8)) multiplexer_3 (.in0(R_DATA2), .in1(IMM), .out(multiplexer_3_out), .sel(ALU_SRC));
  // Probe on IMM
  ULA ula_1 (
    .SRC1(registerfile_1_r_data1), .SRC2(multiplexer_3_out), .ALU_OP(ALU_OP), .BRANCH_FLAG(B_FLAG),
    .ALU_ZERO(ALU_ZERO), .RESULT(ALU_DATA));
  UC uc_1 (
    .OPCODE(OPCODE), .FUNCT(FUNCT), .CLK(CLK), .IMM_SEL(IMM_SEL), .ALU_SRC(ALU_SRC), .ALU_OP(ALU_OP),
    .REG_WRITE(R_WRITE), .BRANCH(uc_1_branch), .JUMP(JUMP), .MEM_TO_REG(MEM_TO_REG), .MEM_READ(MEM_READ),
    .MEM_WRITE(MEM_WRITE));
  DataMemory datamemory_1 (
    .CLK(CLK), .MEM_READ(MEM_READ), .WRITE_ENABLE(MEM_WRITE), .ADDRESS(ALU_DATA), .WRITE_DATA(R_DATA2),
    .READ_DATA(MEM_DATA));
  // Probe on MEM_DATA
  and and_1 (and_1_out, uc_1_branch, B_FLAG);
  or or_1 (PC_SRC, and_1_out, JUMP);
endmodule

module RegisterFile (
  input  CLK,
  input  RST,
  input  [7:0] DATA,
  input  REG_WRITE,
  input  [2:0] RS1,
  input  [2:0] RS2,
  input  [2:0] RD,
  output [7:0] R_DATA1,
  output [7:0] R_DATA2
);

  wire WE_x1, WE_x2, WE_x3, WE_x4, WE_x5, WE_x6, WE_x7;
  wire [7:0] Q_x0, Q_x1, Q_x2, Q_x3, Q_x4, Q_x5, Q_x6, Q_x7;

  Register #(.trigger("falling")) x0 (.D({8{1'b0}}), .clk(CLK), .Q(Q_x0), .clr(RST));  // open: en
  Register #(.trigger("falling")) x4 (.D(DATA), .en(WE_x4), .clk(CLK), .Q(Q_x4), .clr(RST));
  // Probe on DATA
  Register #(.trigger("falling")) x1 (.D(DATA), .en(WE_x1), .clk(CLK), .Q(Q_x1), .clr(RST));
  Register #(.trigger("falling")) x5 (.D(DATA), .en(WE_x5), .clk(CLK), .Q(Q_x5), .clr(RST));
  Demultiplexer #(.select(3)) demultiplexer_1 (
    .out1(WE_x1), .out2(WE_x2), .out3(WE_x3), .out4(WE_x4), .out5(WE_x5), .out6(WE_x6), .out7(WE_x7),
    .in(REG_WRITE), .sel(RD));  // open: out0
  Register #(.trigger("falling")) x2 (.D(DATA), .en(WE_x2), .clk(CLK), .Q(Q_x2), .clr(RST));
  Register #(.trigger("falling")) x6 (.D(DATA), .en(WE_x6), .clk(CLK), .Q(Q_x6), .clr(RST));
  Register #(.trigger("falling")) x3 (.D(DATA), .en(WE_x3), .clk(CLK), .Q(Q_x3), .clr(RST));
  Register #(.trigger("falling")) x7 (.D(DATA), .en(WE_x7), .clk(CLK), .Q(Q_x7), .clr(RST));
  Multiplexer #(.select(3), .width(8)) multiplexer_1 (
    .in0(Q_x0), .in1(Q_x1), .in2(Q_x2), .in3(Q_x3), .in4(Q_x4), .in5(Q_x5), .in6(Q_x6), .in7(Q_x7),
    .out(R_DATA2), .sel(RS2));
  Multiplexer #(.select(3), .width(8)) multiplexer_2 (
    .in0(Q_x0), .in1(Q_x1), .in2(Q_x2), .in3(Q_x3), .in4(Q_x4), .in5(Q_x5), .in6(Q_x6), .in7(Q_x7),
    .out(R_DATA1), .sel(RS1));

  // Other names for the same wires on the sheet: RW = REG_WRITE
endmodule

module InstructionFetch (
  input  CLK,
  input  RST,
  input  PC_SRC,
  input  [7:0] IMM,
  output [15:0] INSTRUCTION,
  output [7:0] LINK_DATA
);

  wire [7:0] adder_2_out, IMM_t, multiplexer_1_out, PC_q;

  Register PC (.D(adder_2_out), .en(1'b1), .clk(CLK), .Q(PC_q), .clr(RST));
  // Probe on IMM
  // Probe on IMM_t
  Shifter shifter_1 (.in(IMM), .\dist (3'b001), .out(IMM_t));
  Multiplexer #(.width(8)) multiplexer_1 (.in0(8'h2), .in1(IMM_t), .out(multiplexer_1_out), .sel(PC_SRC));
  Adder adder_1 (.a(PC_q), .b(8'h2), .out(LINK_DATA));  // open: cin, cout
  Adder adder_2 (.a(multiplexer_1_out), .b(PC_q), .out(adder_2_out));  // open: cin, cout
  // Probe on PC_q
  // Probe on LINK_DATA
  // Probe on adder_2_out
  // ROM #(.line("dual")) rom_1: pin names not known; wires that end beside it: PC_q, INSTRUCTION[15:8], INSTRUCTION[7:0]
  // Probe on INSTRUCTION

  // Notes on the sheet:
  //   contents of rom_1 (hex, n*v repeats v):
  //   0 0 22 a 24 b 26 e 28 f 1a a 1c 14 81 2b 81 34 60 5 e 8e 60 4 e c0 60 2 7e 81 12 14 72 41 74 41 6 50
  //   81 dc 6 c0 60 2 7 c 12 1 4 cd 34 16 34 3f
endmodule

module InstructionDecode (
  input  [15:0] INSTRUCTION,
  output [2:0] RS1,
  output [2:0] RS2,
  output [2:0] RD,
  output [3:0] OPCODE,
  output [2:0] FUNCT,
  output [5:0] I_IMM,
  output [5:0] S_IMM,
  output [5:0] B_IMM,
  output [8:0] J_IMM
);

  // Probe on INSTRUCTION

  assign B_IMM = {INSTRUCTION[11:9], INSTRUCTION[2:0]};
  assign FUNCT = INSTRUCTION[2:0];
  assign I_IMM = INSTRUCTION[5:0];
  assign J_IMM = INSTRUCTION[8:0];
  assign OPCODE = INSTRUCTION[15:12];
  assign RD = INSTRUCTION[11:9];
  assign RS1 = INSTRUCTION[8:6];
  assign RS2 = INSTRUCTION[5:3];
  assign S_IMM = {INSTRUCTION[11:9], INSTRUCTION[2:0]};

  // Notes on the sheet:
  //   I-Type Immediate
  //   B-Type Immediate
  //   S-Type Immediate
  //   J-Type Immediate
endmodule

module ULA (
  input  [7:0] SRC1,
  input  [7:0] SRC2,
  input  [2:0] ALU_OP,
  output BRANCH_FLAG,
  output ALU_ZERO,
  output [7:0] RESULT
);

  wire comparator_2_lt, comparator_3_eq, not_1_out, not_2_out, not_3_out;
  wire [7:0] ADD, BNE, IOR, LAND, LSL, LSR, SLTU, SUB;

  Adder adder_1 (.a(SRC1), .b(SRC2), .out(ADD));  // open: cin, cout
  Subtractor subtractor_1 (.a(SRC1), .b(SRC2), .out(SUB));  // open: bin, bout
  // Probe on SRC1
  // Probe on SRC1
  // Probe on SRC2
  // Probe on ALU_OP
  assign IOR = SRC1 | SRC2;  // OR_Gate or_1, 8 bits wide
  assign LAND = SRC1 & SRC2;  // AND_Gate and_1, 8 bits wide
  Multiplexer #(.select(3), .width(8)) multiplexer_1 (
    .in0(ADD), .in1(SUB), .in2(LAND), .in3(IOR), .in4(SLTU), .in5(LSL), .in6(LSR), .in7(BNE), .out(RESULT),
    .sel(ALU_OP));
  Comparator comparator_1 (.a({8{1'b0}}), .b(RESULT), .eq(ALU_ZERO));  // open: gt, lt
  // Probe on RESULT
  // Probe on RESULT
  Multiplexer #(.select(3)) multiplexer_2 (
    .in1(ALU_ZERO), .in4(not_1_out), .in7(not_2_out), .out(BRANCH_FLAG), .sel(ALU_OP));  // open: in0, in2, in3, in5, in6
  not not_1 (not_1_out, ALU_ZERO);
  not not_2 (not_2_out, ALU_ZERO);
  Comparator #(.mode("unsigned")) comparator_2 (.a(SRC1), .b(SRC2), .lt(comparator_2_lt));  // open: gt, eq
  assign SLTU = {{7{1'b0}}, comparator_2_lt};  // Bit_Extender bit_extender_1
  Shifter shifter_1 (.in(SRC1), .\dist (SRC2[2:0]), .out(LSL));
  Shifter #(.shift("lr")) shifter_2 (.in(SRC1), .\dist (SRC2[2:0]), .out(LSR));
  not not_3 (not_3_out, comparator_3_eq);
  Comparator comparator_3 (.a(SRC1), .b(SRC2), .eq(comparator_3_eq));  // open: gt, lt
  assign BNE = {{7{1'b0}}, not_3_out};  // Bit_Extender bit_extender_2

  // Notes on the sheet:
  //   INPUTS
  //   Addition (ADD)
  //   Subtraction (SUB)
  //   Inclusive OR (IOR/OR)
  //   Logical AND (LAN/AND)
  //   Logical Shift Left (LSL/SLL)
  //   Set Less Than Unsigned (SLTU)
  //   Logical Shift Right  (SRL/LSR)
  //   Branch if Not Equal (BNE)
endmodule

module UC (
  input  [3:0] OPCODE,
  input  [2:0] FUNCT,
  input  CLK,
  output [1:0] IMM_SEL,
  output ALU_SRC,
  output [2:0] ALU_OP,
  output REG_WRITE,
  output BRANCH,
  output JUMP,
  output MEM_TO_REG,
  output MEM_READ,
  output MEM_WRITE
);

  wire B_TYPE_BEQ, B_TYPE_BLT, B_TYPE_BNE, I_IMM, I_TYPE_ADDI, I_TYPE_SLLI, R_TYPE;
  wire [2:0] or_1_out;

  Decoder #(.select(4)) decoder_1 (
    .out0(R_TYPE), .out1(I_TYPE_ADDI), .out2(MEM_READ), .out3(MEM_WRITE), .out4(B_TYPE_BEQ),
    .out5(B_TYPE_BNE), .out6(JUMP), .out7(I_TYPE_SLLI), .out8(B_TYPE_BLT), .sel(OPCODE), .en(1'b1));  // open: out9, out10, out11, out12, out13, out14, out15
  or or_1 (or_1_out[0], B_TYPE_BNE, B_TYPE_BEQ, I_TYPE_SLLI);
  or or_2 (or_1_out[2], B_TYPE_BLT, B_TYPE_BNE, I_TYPE_SLLI);
  or or_3 (I_IMM, MEM_READ, I_TYPE_ADDI, I_TYPE_SLLI);
  or or_4 (BRANCH, B_TYPE_BLT, B_TYPE_BEQ, B_TYPE_BNE);
  or or_5 (REG_WRITE, R_TYPE, JUMP, I_IMM);
  // Probe on {or_1_out[2], B_TYPE_BNE, or_1_out[0]}
  // Probe on ALU_OP
  Multiplexer #(.width(3)) multiplexer_1 (
    .in0({or_1_out[2], B_TYPE_BNE, or_1_out[0]}), .in1(FUNCT), .out(ALU_OP), .sel(R_TYPE));
  // Probe on IMM_SEL
  or or_6 (IMM_SEL[0], MEM_WRITE, JUMP);
  or or_7 (IMM_SEL[1], BRANCH, JUMP);
  or or_8 (ALU_SRC, MEM_WRITE, I_IMM);

  assign MEM_TO_REG = MEM_READ;

  // Other names for the same wires on the sheet: B_IMM = BRANCH; I_TYPE_LOAD = MEM_READ; J_TYPE = JUMP;
  //   S_TYPE = MEM_WRITE

  // Notes on the sheet:
  //   INPUTS
  //   REG_WRITE
  //   ALU_OP
  //   IMM_SEL
  //   ALU_SRC
  //   OUTPUTS
endmodule

module ImmGen (
  input  [5:0] I_IMM,
  input  [5:0] S_IMM,
  input  [5:0] B_IMM,
  input  [8:0] J_IMM,
  input  [1:0] IMM_SEL,
  output [7:0] IMM
);

  wire [7:0] B_IMM_t, I_IMM_t, S_IMM_t;

  // Probe on IMM
  Multiplexer #(.select(2), .width(8)) multiplexer_1 (
    .in0(I_IMM_t), .in1(S_IMM_t), .in2(B_IMM_t), .in3(J_IMM[7:0]), .out(IMM), .sel(IMM_SEL));
  assign I_IMM_t = {{2{I_IMM[5]}}, I_IMM};  // Bit_Extender bit_extender_1
  assign S_IMM_t = {{2{S_IMM[5]}}, S_IMM};  // Bit_Extender bit_extender_2
  assign B_IMM_t = {{2{B_IMM[5]}}, B_IMM};  // Bit_Extender bit_extender_3

  // Other names for the same wires on the sheet: J_IMM_t[7:0] = J_IMM[7:0]
endmodule

module DataMemory (
  input  CLK,
  input  MEM_READ,
  input  WRITE_ENABLE,
  input  [7:0] ADDRESS,
  input  [7:0] WRITE_DATA,
  output [7:0] READ_DATA
);

  wire [7:0] ram_1_dout;

  // Probe on ADDRESS
  // Probe on ADDRESS
  // Probe on WRITE_DATA
  // Probe on WRITE_DATA
  // Probe on ADDRESS
  // Probe on ADDRESS
  RAM #(.asyncread("true")) ram_1 (
    .addr(ADDRESS), .we(WRITE_ENABLE), .oe(MEM_READ), .clk(CLK), .din(WRITE_DATA), .dout(ram_1_dout));
  // Probe on READ_DATA
  assign READ_DATA = MEM_READ ? ram_1_dout : 8'bz;  // Controlled_Buffer controlled_buffer_1
  // Probe on READ_DATA

  // Other names for the same wires on the sheet: ME = MEM_READ; WE = WRITE_ENABLE
endmodule
